# Fritzing sketch Pinball Inputs (saved by Fritzing 0.7.7b)
breadboards: 1

parts:
  U20 = IC, DIP package, 14 pins [chip_label=LM339]
  S18 = Resistor [tolerance=±5% resistance=10k package=THT]
  S26 = Resistor [tolerance=±5% resistance=10k package=THT]
  S17 = Resistor [tolerance=±5% resistance=10k package=THT]
  S25 = Resistor [tolerance=±5% resistance=10k package=THT]
  S37 = Resistor [tolerance=±5% resistance=4.7k package=THT]
  S36 = Resistor [tolerance=±5% resistance=4.7k package=THT]
  S35 = Resistor [tolerance=±5% resistance=4.7k package=THT]
  S34 = Resistor [tolerance=±5% resistance=4.7k package=THT]
  R18 = Resistor [tolerance=±5% resistance=10k package=THT]
  R19 = Resistor [tolerance=±5% resistance=4.7k package=THT]
  R27 = Resistor [tolerance=±5% resistance=4.7k package=THT]
  R26 = Resistor [tolerance=±5% resistance=4.7k package=THT]
  R25 = Resistor [tolerance=±5% resistance=4.7k package=THT]
  R24 = Resistor [tolerance=±5% resistance=4.7k package=THT]
  S13 = Resistor [tolerance=±5% resistance=10k package=THT]
  S15 = Resistor [tolerance=±5% resistance=10k package=THT]
  S16 = Resistor [tolerance=±5% resistance=10k package=THT]
  S32 = Resistor [tolerance=±5% resistance=4.7k package=THT]
  S33 = Resistor [tolerance=±5% resistance=4.7k package=THT]
  S38 = Resistor [tolerance=±5% resistance=4.7k package=THT]
  S39 = Resistor [tolerance=±5% resistance=4.7k package=THT]
  R20 = Resistor [tolerance=±5% resistance=4.7k package=THT]
  R21 = Resistor [tolerance=±5% resistance=4.7k package=THT]
  R23 = Resistor [tolerance=±5% resistance=4.7k package=THT]
  R22 = Resistor [tolerance=±5% resistance=4.7k package=THT]
  S24 = Resistor [tolerance=±5% resistance=10k package=THT]
  S25_2 = Resistor [tolerance=±5% resistance=10k package=THT]
  S12 = Resistor [tolerance=±5% resistance=10k package=THT]
  R17 = Resistor [tolerance=±5% resistance=3.3k package=THT]
  R15 = Resistor [tolerance=±5% resistance=3.3k package=THT]
  R16 = Resistor [tolerance=±5% resistance=3.3k package=THT]
  R13 = Resistor [tolerance=±5% resistance=2.2k package=THT]
  R12 = Resistor [tolerance=±5% resistance=2.2k package=THT]
  R14 = Resistor [tolerance=±5% resistance=2.2k package=THT]
  D4 = Rectifier Diode [part_number=1N414B package="300 mil [THT]"]
  D3 = Rectifier Diode [part_number=1N414B package="300 mil [THT]"]
  C39 = Ceramic Capacitor [capacitance=10nF voltage=50V package="100 mil [THT, multilayer]"]
  C37 = Ceramic Capacitor [capacitance=10nF voltage=50V package="100 mil [THT, multilayer]"]
  C35 = Ceramic Capacitor [capacitance=10nF voltage=50V package="100 mil [THT, multilayer]"]
  C34 = Ceramic Capacitor [capacitance=10nF voltage=50V package="100 mil [THT, multilayer]"]
  C36 = Ceramic Capacitor [capacitance=10nF voltage=50V package="100 mil [THT, multilayer]"]
  C33 = Ceramic Capacitor [capacitance=10nF voltage=50V package="100 mil [THT, multilayer]"]
  C32 = Ceramic Capacitor [capacitance=10nF voltage=50V package="100 mil [THT, multilayer]"]
  C31 = Ceramic Capacitor [capacitance=10nF voltage=50V package="100 mil [THT, multilayer]"]
  C30 = Ceramic Capacitor [capacitance=10nF voltage=50V package="100 mil [THT, multilayer]"]
  C26 = Ceramic Capacitor [capacitance=10nF voltage=50V package="100 mil [THT, multilayer]"]
  C25 = Ceramic Capacitor [capacitance=10nF voltage=50V package="100 mil [THT, multilayer]"]
  C27 = Ceramic Capacitor [capacitance=10nF voltage=50V package="100 mil [THT, multilayer]"]
  U21 = IC, DIP package, 14 pins [chip_label=LM339]
  U19 = IC, DIP package, 14 pins [chip_label=LM339]
  SLM_TLT_TST = female pin header, 3 pins [form="♀ (female)"]
  +5VDC = female pin header, 2 pins [form="♀ (female)"]
  RET7-RET4 = female pin header, 4 pins [form="♀ (female)"]
  RET3-RET0 = female pin header, 4 pins [form="♀ (female)"]
  S14 = Resistor [tolerance=±5% resistance=10k package=THT]
  D5 = Rectifier Diode [part_number=1N4001 breakdown_voltage=3.6V package="300 mil [THT]"]
  Pad1 = Pad [width=4.5 height=4.5 connect=center]  # not connected
  Pad2 = Pad [width=4.5 height=4.5 connect=center]  # not connected
  Pad3 = Pad [width=4.5 height=4.5 connect=center]
  Pad4 = Pad [width=4.5 height=4.5 connect=center]

nets:
  N1: U20.pin1, S17.Pin_1, RET7-RET4.pin1
  N2: U20.pin2, S18.Pin_1, RET7-RET4.pin2
  N3: U20.pin3, S18.Pin_0, S26.Pin_0, S17.Pin_0, S25.Pin_0, R18.Pin_0, S13.Pin_0, S15.Pin_0, S16.Pin_0, S24.Pin_0, S25_2.Pin_0, S12.Pin_0, R13.Pin_0, R12.Pin_0, R14.Pin_0, U21.pin3, U19.pin3, +5VDC.pin1, S14.Pin_0
  N4: U20.pin4, S37.Pin_1, R25.Pin_1, C35.1
  N5: U20.pin5, U20.pin7, U20.pin9, U20.pin11, R18.Pin_1, R19.Pin_1, C39.0, U21.pin5, U21.pin7, U21.pin9, U19.pin5, U19.pin7, U19.pin9, U19.pin11
  N6: U20.pin6, S36.Pin_1, R24.Pin_1, C34.1
  N7: U20.pin8, S35.Pin_1, R26.Pin_1, C36.0
  N8: U20.pin10, S34.Pin_1, R27.Pin_1, C37.0
  N9: U20.pin12, S37.Pin_0, S36.Pin_0, S35.Pin_0, S34.Pin_0, R19.Pin_0, S32.Pin_0, S33.Pin_0, S38.Pin_0, S39.Pin_0, C39.1, C37.1, C35.0, C34.0, C36.1, C33.1, C32.1, C31.0, C30.0, C26.0, C25.0, C27.1, U21.pin12, U19.pin12, +5VDC.pin2, Pad3.pad, Pad4.pad
  N10: U20.pin13, S25.Pin_1, RET7-RET4.pin4
  N11: U20.pin14, S26.Pin_1, RET7-RET4.pin3
  N12: S13.Pin_1, U19.pin1, RET3-RET0.pin1
  N13: S15.Pin_1, U19.pin14, RET3-RET0.pin3
  N14: S16.Pin_1, U19.pin13, RET3-RET0.pin4
  N15: S32.Pin_1, R21.Pin_1, C30.1, U19.pin4
  N16: S33.Pin_1, R20.Pin_1, C31.1, U19.pin6
  N17: S38.Pin_1, R23.Pin_1, C33.0, U19.pin10
  N18: S39.Pin_1, R22.Pin_1, C32.0, U19.pin8
  N19: S24.Pin_1, U21.pin1, SLM_TLT_TST.pin1
  N20: S25_2.Pin_1, U21.pin2, SLM_TLT_TST.pin2
  N21: S12.Pin_1, U21.pin14, SLM_TLT_TST.pin3
  N22: R17.Pin_0, R14.Pin_1, C27.0, D5.anode
  N23: R17.Pin_1, U21.pin8
  N24: R15.Pin_0, R12.Pin_1, D3.anode, C25.1
  N25: R15.Pin_1, U21.pin6
  N26: R16.Pin_0, R13.Pin_1, D4.anode, C26.1
  N27: R16.Pin_1, U21.pin4
  N28: U19.pin2, RET3-RET0.pin2, S14.Pin_1
